# Fritzing sketch sketch_pong32x32-sd (saved by Fritzing 1.0.6)

parts:
  esp1 = ESP32 DevKitc V4
  microSD1 = MicroSD Card Module
  LLC1 = Logic Level Converter [package="Breakout board"]

nets:
  N1: esp1.IO5, LLC1.LV4
  N2: esp1.IO18, LLC1.LV3
  N3: esp1.IO19, LLC1.LV1
  N4: esp1.IO23, LLC1.LV2
  GND: esp1.GND, microSD1.GND
  N5: esp1.3V3, LLC1.LV
  5V: esp1.5V, microSD1.VCC
  N6: microSD1.MISO, LLC1.HV1
  N7: microSD1.MOSI, LLC1.HV2
  N8: microSD1.SCK, LLC1.HV3
  N9: microSD1.CS, LLC1.HV4

custom parts:
  ESP32 DevKitc V4: ESP32-DevKitC board with ESP32-WROOM-32 module. ESP32-DevKitC V4 is a small-sized ESP32-based development board produced by Espressif. Most of the pins on the ESP module are broken out to the pin headers on the board. The pins D0, D1, D2, D3, CMD and CLK are used internally for communication between ESP32 and SPI flash memory. They are grouped on both sides near the USB connector. Avoid using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
  Logic Level Converter: 5V to/from 3.3V logic level converter
