# Fritzing sketch sketch_pong32x32_audio (saved by Fritzing 1.0.6)

parts:
  esp1 = ESP32 DevKitc V4
  DFRobot_DFPlayer_Mini1 = DFRobot DFPlayer Mini [part_number=DFR0299]
  SP1 = SPEAKER [package=pcb_mount_speaker]

nets:
  N1: esp1.IO4, DFRobot_DFPlayer_Mini1.TX
  N2: esp1.GND, DFRobot_DFPlayer_Mini1.GND-1
  N3: esp1.IO13, DFRobot_DFPlayer_Mini1.RX
  N4: DFRobot_DFPlayer_Mini1.SPK_1, SP1.-
  N5: DFRobot_DFPlayer_Mini1.SPK_2, SP1.+

custom parts:
  ESP32 DevKitc V4: ESP32-DevKitC board with ESP32-WROOM-32 module. ESP32-DevKitC V4 is a small-sized ESP32-based development board produced by Espressif. Most of the pins on the ESP module are broken out to the pin headers on the board. The pins D0, D1, D2, D3, CMD and CLK are used internally for communication between ESP32 and SPI flash memory. They are grouped on both sides near the USB connector. Avoid using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
