# Fritzing sketch sketch_pong32x32_joy (saved by Fritzing 1.0.6)

parts:
  esp1 = ESP32 DevKitc V4
  Mod1 = KY-023 Dual Axis Joystick Module [package="Breakout board"]
  Mod2 = KY-023 Dual Axis Joystick Module [package="Breakout board"]

nets:
  +5V: esp1.3V3, Mod1.+5V, Mod2.+5V
  N1: esp1.IO34, Mod1.VRy
  N2: esp1.IO35, Mod1.VRx
  N3: esp1.IO32, Mod2.VRx
  N4: esp1.IO33, Mod2.VRy
  N5: esp1.IO26, Mod2.SW
  N6: esp1.IO27, Mod1.SW
  GND: esp1.GND, Mod1.GND, Mod2.GND

custom parts:
  ESP32 DevKitc V4: ESP32-DevKitC board with ESP32-WROOM-32 module. ESP32-DevKitC V4 is a small-sized ESP32-based development board produced by Espressif. Most of the pins on the ESP module are broken out to the pin headers on the board. The pins D0, D1, D2, D3, CMD and CLK are used internally for communication between ESP32 and SPI flash memory. They are grouped on both sides near the USB connector. Avoid using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
  KY-023 Dual Axis Joystick Module: KY-023 Dual-Axis Joystick Module.
