# Fritzing sketch sketch_pong32x32_lcd_encoder (saved by Fritzing 1.0.6)

parts:
  esp1 = ESP32 DevKitc V4
  RE1 = KY-040 Rotary encoder [package=THT]
  Bauteil1 = LCD1602-I2C

nets:
  N1: esp1.IO16, RE1.DT
  N2: esp1.IO17, RE1.SW
  N3: esp1.IO21, Bauteil1.SDA
  N4: esp1.IO22, Bauteil1.SCL
  3V3: esp1.3V3, RE1.Vcc
  N5: esp1.IO25, RE1.CLK
  GND: esp1.GND, RE1.GND

custom parts:
  ESP32 DevKitc V4: ESP32-DevKitC board with ESP32-WROOM-32 module. ESP32-DevKitC V4 is a small-sized ESP32-based development board produced by Espressif. Most of the pins on the ESP module are broken out to the pin headers on the board. The pins D0, D1, D2, D3, CMD and CLK are used internally for communication between ESP32 and SPI flash memory. They are grouped on both sides near the USB connector. Avoid using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
  KY-040 Rotary encoder: KY-040 Rotary Encoder with switch on breakout borad from AZ Delivery
  LCD1602-I2C: A standard character display, usually with 2x16 characters. Comes in many colors with LCM1602 IIC attached.
