# Fritzing sketch sketch_pong32x32_matrix (saved by Fritzing 1.0.6)

parts:
  esp1 = ESP32 DevKitc V4
  Bauteil1 = Matrix LED de 8x8 basada en MAX7219
  Bauteil2 = Matrix LED de 8x8 basada en MAX7219
  Bauteil3 = Matrix LED de 8x8 basada en MAX7219
  Bauteil4 = Matrix LED de 8x8 basada en MAX7219
  Bauteil5 = NeoPixel NeoMatrix 8x8 [part_number=1487]
  Bauteil6 = NeoPixel NeoMatrix 8x8 [part_number=1487]

nets:
  N1: esp1.IO15, Bauteil4.CS
  N2: esp1.IO18, Bauteil4.CLK
  N3: esp1.IO23, Bauteil4.DIN
  N4: esp1.GND, Bauteil4.GND#1
  3V3: esp1.3V3, Bauteil4.VCC
  N5: esp1.IO14, Bauteil5.IN
  N6: Bauteil1.VCC, Bauteil4.VCC(OUT)
  N7: Bauteil1.GND#1, Bauteil4.GND#6
  N8: Bauteil1.CS, Bauteil4.CS(OUT)
  N9: Bauteil1.CLK, Bauteil4.CLK(OUT)
  N10: Bauteil1.DIN, Bauteil4.DOUT
  N11: Bauteil1.VCC(OUT), Bauteil2.VCC
  N12: Bauteil1.GND#6, Bauteil2.GND#1
  N13: Bauteil1.CS(OUT), Bauteil2.CS
  N14: Bauteil1.CLK(OUT), Bauteil2.CLK
  N15: Bauteil1.DOUT, Bauteil2.DIN
  N16: Bauteil2.VCC(OUT), Bauteil3.VCC
  N17: Bauteil2.GND#6, Bauteil3.GND
  N18: Bauteil2.CS(OUT), Bauteil3.CS
  N19: Bauteil2.CLK(OUT), Bauteil3.CLK
  N20: Bauteil2.DOUT, Bauteil3.DIN
  VDD: Bauteil5.VDD, Bauteil6.VDD
  GND: Bauteil5.GND, Bauteil6.GND
  N21: Bauteil5.OUT, Bauteil6.IN

notes:
  5 Volt, 10 Ampere Power Supply
  Each matrix must be connected to this power supply. Keep in mind: each matrix may consume 3.5 Watt depending on
  Matrix 1 of 16
  Matrix 2 of 16
  Keeping the things simple only 2 of 16 matrix elements are shown here. Alle elements must be connected sequentially in the same way.

custom parts:
  ESP32 DevKitc V4: ESP32-DevKitC board with ESP32-WROOM-32 module. ESP32-DevKitC V4 is a small-sized ESP32-based development board produced by Espressif. Most of the pins on the ESP module are broken out to the pin headers on the board. The pins D0, D1, D2, D3, CMD and CLK are used internally for communication between ESP32 and SPI flash memory. They are grouped on both sides near the USB connector. Avoid using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
  NeoPixel NeoMatrix 8x8: Put on your sunglasses before wiring up this LED matrix - 64 eye-blistering RGB LEDs adorn the NeoMatrix for a blast of configurable color. Arranged in an 8x8 matrix, each pixel is individually addressable. Only one microcontroller pin is required to control all the LEDs, and you get 24 bit color for each LED.
